// Logisim project DMA_CONTROLLER_LOGISIM.circ as structural Verilog: 1 circuit, main circuit main
module main (
  input  START,
  input  BUS_GRANT,
  output Bus_Request,
  output [7:0] Address_Output,
  output [7:0] Transferred_Data
);

  wire and_1_out, clock_1_out;

  Clock clock_1 (.out(clock_1_out));
  D_Flip_Flop d_ff_1 (.clk(clock_1_out), .D(START), .Q(Bus_Request));  // open: Qn, preset, en, reset
  and and_1 (and_1_out, Bus_Request, clock_1_out, BUS_GRANT);
  Counter counter_1 (.Q(Address_Output), .clk(and_1_out));  // open: load, D, count, carry, clr
  ROM rom_1 (.addr(Address_Output), .data(Transferred_Data));  // open: sel

  // Notes on the sheet:
  //   contents of rom_1 (hex, n*v repeats v):
  //   1 2 3 4 5 6 7 8 9 10 11 12 13 14 15 16
endmodule
